// Logisim project cpu.circ as structural Verilog: 1 circuit, main circuit cpu
module cpu (
  input  clk,
  input  [31:0] Instruction,
  input  [31:0] MemReadData,
  output [31:0] MemAddress,
  output [31:0] ProgramCounter,
  output [31:0] ra,
  output [31:0] sp,
  output [31:0] t0,
  output [31:0] t1,
  output [31:0] t2,
  output [31:0] s0,
  output [31:0] s1,
  output [31:0] a0,
  output [3:0] MemWriteMask,
  output [31:0] MemWriteData
);

  wire ASel, BrEq, BrLt, BSel, control_logic_1_brun, MemWEn, PCSel, RegWen;
  wire [1:0] WBSel;
  wire [2:0] ImmSel;
  wire [3:0] ALUSel;
  wire [31:0] adder_1_out, adder_2_out, ALUA, ALUB, DataToReg, Immediate, multiplexer_1_out,
       multiplexer_2_out, PIPIns, PIPpc, ReadData1, ReadData2, WriteDataReg;

  Adder #(.width(32)) adder_1 (.a(ProgramCounter), .b(32'h4), .out(adder_1_out));  // open: cin, cout
  Multiplexer #(.width(32)) multiplexer_1 (.in0(adder_1_out), .in1(MemAddress), .out(multiplexer_1_out), .sel(PCSel));
  Register #(.width(32)) register_1 (.D(multiplexer_1_out), .clk(clk), .Q(ProgramCounter));  // open: en, clr
  Register #(.width(32)) register_2 (.D(ProgramCounter), .clk(clk), .Q(PIPpc));  // open: en, clr
  Multiplexer #(.width(32)) multiplexer_2 (.in0(Instruction), .in1(32'h13), .out(multiplexer_2_out), .sel(PCSel));
  Adder #(.width(32)) adder_2 (.a(PIPpc), .b(32'h4), .out(adder_2_out));  // open: cin, cout
  Register #(.width(32)) register_3 (.D(multiplexer_2_out), .clk(clk), .Q(PIPIns));  // open: en, clr
  Multiplexer #(.select(2), .width(32)) multiplexer_3 (
    .in0(adder_2_out), .in1(MemAddress), .in2(DataToReg), .out(WriteDataReg), .sel(WBSel));  // open: in3
  control_logic control_logic_1 (
    .Instruction(PIPIns), .BrEq(BrEq), .BrLt(BrLt), .PCSel(PCSel), .RegWEn(RegWen), .ImmSel(ImmSel),
    .BrUn(control_logic_1_brun), .ASel(ASel), .BSel(BSel), .ALUSel(ALUSel), .MemWEn(MemWEn), .WBSel(WBSel));
  regfile regfile_1 (
    .ReadIndex1(PIPIns[19:15]), .ReadIndex2(PIPIns[24:20]), .WriteIndex(PIPIns[11:7]),
    .WriteData(WriteDataReg), .RegWEn(RegWen), .clk(clk), .ra(ra), .sp(sp), .t0(t0), .t1(t1), .t2(t2),
    .s0(s0), .s1(s1), .a0(a0), .ReadData1(ReadData1), .ReadData2(ReadData2));
  imm_gen imm_gen_1 (.Instruction(PIPIns), .ImmSel(ImmSel), .Immediate(Immediate));
  Multiplexer #(.width(32)) multiplexer_4 (.in0(ReadData1), .in1(PIPpc), .out(ALUA), .sel(ASel));
  Multiplexer #(.width(32)) multiplexer_5 (.in0(ReadData2), .in1(Immediate), .out(ALUB), .sel(BSel));
  alu alu_1 (.A(ALUA), .B(ALUB), .ALUSel(ALUSel), .ALUResult(MemAddress));
  branch_comp branch_comp_1 (
    .BrData1(ReadData1), .BrData2(ReadData2), .BrUn(control_logic_1_brun), .BrEq(BrEq), .BrLt(BrLt));
  partial_store partial_store_1 (
    .Instruction(PIPIns), .MemAddress(MemAddress), .DataFromReg(ReadData2), .MemWEn(MemWEn),
    .MemWriteMask(MemWriteMask), .DataToMem(MemWriteData));
  partial_load partial_load_1 (
    .Instruction(PIPIns), .MemAddress(MemAddress), .DataFromMem(MemReadData), .DataToReg(DataToReg));

  // Other names for the same wires on the sheet: ALUResult[31:0] = MemAddress

  // Notes on the sheet:
  //   Piplined Variables
  //   To IMEM
  //   IMEM (do **NOT** move this)
  //   From IMEM
  //   Inputs/Outputs for testing. Do **NOT** move these.
  //   It is OK to move the PC, RegFile, ALU, MEM, Branch Comp, Imm Gen, Partial Load, Partial Store and Control Logic to wherever is most convenient for you when constructing your CPU, and to delete this text
  //   To DMEM
  //   DMEM (do **NOT** move this)
  //   From DMEM
endmodule
