// Logisim project partial-load.circ as structural Verilog: 1 circuit, main circuit partial_load
module partial_load (
  input  [31:0] Instruction,
  input  [31:0] MemAddress,
  input  [31:0] DataFromMem,
  output [31:0] DataToReg
);

  wire comparator_2_eq, comparator_2_gt, comparator_2_lt, is_lb, is_lh, is_lw, LOAD;
  wire [7:0] multiplexer_1_out;
  wire [15:0] multiplexer_2_out;
  wire [31:0] and_4_out, and_5_out, and_6_out, bit_extender_1_out, bit_extender_2_out, bit_extender_3_out,
       lb, lh;

  Comparator #(.width(7)) comparator_1 (.a(7'b0000011), .b(Instruction[6:0]), .eq(LOAD));  // open: gt, lt
  Comparator #(.width(3)) comparator_2 (
    .a(3'b001), .b(Instruction[14:12]), .gt(comparator_2_gt), .eq(comparator_2_eq), .lt(comparator_2_lt));
  and and_1 (is_lb, LOAD, comparator_2_gt);
  and and_2 (is_lh, comparator_2_eq, LOAD);
  and and_3 (is_lw, comparator_2_lt, LOAD);
  assign and_4_out = lb & bit_extender_1_out;  // AND_Gate and_4, 32 bits wide
  assign bit_extender_1_out = {{31{is_lb}}, is_lb};  // Bit_Extender bit_extender_1
  assign and_5_out = lh & bit_extender_2_out;  // AND_Gate and_5, 32 bits wide
  assign bit_extender_2_out = {{31{is_lh}}, is_lh};  // Bit_Extender bit_extender_2
  assign bit_extender_3_out = {{31{is_lw}}, is_lw};  // Bit_Extender bit_extender_3
  assign and_6_out = DataFromMem & bit_extender_3_out;  // AND_Gate and_6, 32 bits wide
  Multiplexer #(.select(2), .width(8)) multiplexer_1 (
    .in0(DataFromMem[7:0]), .in1(DataFromMem[15:8]), .in2(DataFromMem[23:16]), .in3(DataFromMem[31:24]),
    .out(multiplexer_1_out), .sel(MemAddress[1:0]));
  Multiplexer #(.select(2), .width(16)) multiplexer_2 (
    .in0(DataFromMem[15:0]), .in1(DataFromMem[23:8]), .in2(DataFromMem[31:16]), .out(multiplexer_2_out),
    .sel(MemAddress[1:0]));  // open: in3
  assign lb = {{24{multiplexer_1_out[7]}}, multiplexer_1_out};  // Bit_Extender bit_extender_4
  assign lh = {{16{multiplexer_2_out[15]}}, multiplexer_2_out};  // Bit_Extender bit_extender_5
  assign DataToReg = and_4_out | and_5_out | and_6_out;  // OR_Gate or_1, 32 bits wide

  // Other names for the same wires on the sheet: op[6:0] = Instruction[6:0]; func3[2:0] = Instruction[14:12];
  //   MemLast2[1:0] = MemAddress[1:0]

  // Notes on the sheet:
  //   INPUTS to your circuit
  //   DON'T CHANGE THE LOCATIONS OF THE INPUTS AND OUTPUTS!
  //   OUTPUT from your circuit
endmodule
