// Logisim project partial-store.circ as structural Verilog: 1 circuit, main circuit partial_store
module partial_store (
  input  [31:0] Instruction,
  input  [31:0] MemAddress,
  input  [31:0] DataFromReg,
  input  MemWEn,
  output [3:0] MemWriteMask,
  output [31:0] DataToMem
);

  wire comparator_2_eq, comparator_2_gt, comparator_2_lt, is_sb, is_sh, is_sw, STORE;
  wire [3:0] and_8_out, and_9_out, and_10_out, bit_extender_4_out, bit_extender_5_out, bit_extender_6_out,
       bit_extender_7_out, bit_extender_8_out, bit_extender_9_out, sb_mask, sh_mask;
  wire [31:0] and_5_out, and_6_out, and_7_out, bit_extender_1_out, bit_extender_2_out, bit_extender_3_out,
       sb, sh;

  Comparator #(.width(7)) comparator_1 (.a(7'b0100011), .b(Instruction[6:0]), .eq(STORE));  // open: gt, lt
  Comparator #(.width(3)) comparator_2 (
    .a(3'b001), .b(Instruction[14:12]), .gt(comparator_2_gt), .eq(comparator_2_eq), .lt(comparator_2_lt));
  Multiplexer #(.select(2), .width(32)) multiplexer_1 (
    .in0({{24{1'b0}}, DataFromReg[7:0]}), .in1({{16{1'b0}}, DataFromReg[7:0], {8{1'b0}}}),
    .in2({{8{1'b0}}, DataFromReg[7:0], {16{1'b0}}}), .in3({DataFromReg[7:0], {24{1'b0}}}), .out(sb),
    .sel(MemAddress[1:0]));
  Multiplexer #(.select(2), .width(32)) multiplexer_2 (
    .in0({{16{1'b0}}, DataFromReg[15:0]}), .in2({DataFromReg[15:0], {16{1'b0}}}), .out(sh),
    .sel(MemAddress[1:0]));  // open: in1, in3
  and and_1 (is_sb, STORE, comparator_2_gt);
  and and_2 (is_sw, STORE, comparator_2_lt);
  and and_3 (is_sh, comparator_2_eq, STORE);
  // AND_Gate and_4 is placed but not wired
  assign bit_extender_1_out = {{31{is_sb}}, is_sb};  // Bit_Extender bit_extender_1
  assign bit_extender_2_out = {{31{is_sh}}, is_sh};  // Bit_Extender bit_extender_2
  assign bit_extender_3_out = {{31{is_sw}}, is_sw};  // Bit_Extender bit_extender_3
  assign bit_extender_4_out = {{3{is_sb}}, is_sb};  // Bit_Extender bit_extender_4
  assign bit_extender_5_out = {{3{MemWEn}}, MemWEn};  // Bit_Extender bit_extender_5
  assign bit_extender_6_out = {{3{is_sh}}, is_sh};  // Bit_Extender bit_extender_6
  assign bit_extender_7_out = {{3{MemWEn}}, MemWEn};  // Bit_Extender bit_extender_7
  assign bit_extender_8_out = {{3{is_sw}}, is_sw};  // Bit_Extender bit_extender_8
  assign bit_extender_9_out = {{3{MemWEn}}, MemWEn};  // Bit_Extender bit_extender_9
  assign and_5_out = sb & bit_extender_1_out;  // AND_Gate and_5, 32 bits wide
  assign and_6_out = sh & bit_extender_2_out;  // AND_Gate and_6, 32 bits wide
  assign and_7_out = bit_extender_3_out & DataFromReg;  // AND_Gate and_7, 32 bits wide
  assign and_8_out = bit_extender_4_out & bit_extender_5_out & sb_mask;  // AND_Gate and_8, 4 bits wide
  assign and_9_out = bit_extender_6_out & bit_extender_7_out & sh_mask;  // AND_Gate and_9, 4 bits wide
  assign and_10_out = bit_extender_8_out & bit_extender_9_out & 4'b1111;  // AND_Gate and_10, 4 bits wide
  assign MemWriteMask = and_8_out | and_9_out | and_10_out;  // OR_Gate or_1, 4 bits wide
  Multiplexer #(.select(2), .width(4)) multiplexer_3 (
    .in0(4'b0001), .in1(4'b0010), .in2(4'b0100), .in3(4'b1000), .out(sb_mask), .sel(MemAddress[1:0]));
  Multiplexer #(.select(2), .width(4)) multiplexer_4 (
    .in0(4'b0011), .in1(4'b0011), .in2(4'b1100), .in3(4'b1100), .out(sh_mask), .sel(MemAddress[1:0]));
  assign DataToMem = and_5_out | and_6_out | and_7_out;  // OR_Gate or_2, 32 bits wide

  // Other names for the same wires on the sheet: op[6:0] = Instruction[6:0]; func3[2:0] = Instruction[14:12];
  //   MemLast2[1:0] = MemAddress[1:0]

  // Notes on the sheet:
  //   INPUTS to your circuit
  //   DON'T CHANGE THE LOCATIONS OF THE INPUTS AND OUTPUTS!
  //   OUTPUT from your circuit
endmodule
